# Fritzing sketch schematics (saved by Fritzing 0.9.3b)

parts:
  Mosfet_driver_module1 = IFR520 MOS module [package=THT]
  J1 = Power Jack [package=power_jack_smd]
  Raspberry_Pi_1 = Raspberry Pi 3 [part_number=RPI-3-V1.2]
  U2 = LM2596 step down module
  JP2 = Header 2 [package=screwterminal-3.5mm-2_lock]
  Part1 = Adafruit BME280
  DC1 = DC_DC_XL4016 [package=board_screw]
  Mosfet_driver_module3 = IFR520 MOS module [package=THT]
  JP3 = Header 2 [package=screwterminal-3.5mm-2_lock]

nets:
  N1: Mosfet_driver_module1.pin1, Raspberry_Pi_1.GIPO18
  5V: Mosfet_driver_module1.pin2, Raspberry_Pi_1.5V, U2.OUT+, Part1.VIN, Mosfet_driver_module3.pin2
  GND: Mosfet_driver_module1.pin3, Mosfet_driver_module1.pin7, Raspberry_Pi_1.GND, U2.IN-, U2.OUT-, Part1.GND, DC1.OUT-, Mosfet_driver_module3.pin3, Mosfet_driver_module3.pin7
  N2: Mosfet_driver_module1.pin4, JP2.1
  N3: Mosfet_driver_module1.pin5, JP2.2
  N4: Mosfet_driver_module1.pin6, U2.IN+, DC1.OUT+, Mosfet_driver_module3.pin6
  N5: J1.GND, DC1.IN-
  N6: J1.GNDBREAK, DC1.IN+
  N7: Raspberry_Pi_1.GPIO2, Part1.SCK/SCL
  N8: Raspberry_Pi_1.GPIO3, Part1.SDI/SDA
  N9: Raspberry_Pi_1.GIPO23, Mosfet_driver_module3.pin1
  N10: Mosfet_driver_module3.pin4, JP3.1
  N11: Mosfet_driver_module3.pin5, JP3.2

notes:
  Ventilator
  Old ThinkPad DC Power Supply (90 W, 20 V)
  5 V
  max. 6,5 A
  needs ~ 8 A @ 12 V (100 W)
  draws 5 A @ 8 V
  12 V, max. 9 A
  20 V, max. 4,5 A = max. 90 W
  12 V
  20 V
  Heating
  5 V, max. 2 A

custom parts:
  IFR520 MOS module: Breakout board for the IFR520 MOSFET transistor. The module is designed to switch heavy DC loads from a single digital pin of your microcontroller. Its main purpose is to provide a low cost way to drive a DC motor for robotics applications, but the module can be used to control most high current DC loads. Screw terminals are provided to interface to your load and external power source. An LED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
  LM2596 step down module: LM2596 DC-DC step down power supply module 3 A.
  Adafruit BME280: Bosch has stepped up their game with their new BME280 sensor, an environmental sensor with temperature, barometric pressure and humidity! This sensor is great for all sorts of weather/environmental sensing and can even be used in both I2C and SPI! This precision sensor from Bosch is the best low-cost sensing solution for measuring humidity with ±3% accuracy, barometric pressure with ±1 hPa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
